# Fritzing sketch board1 (saved by Fritzing 0.9.3b)

parts:
  Part3 = Arduino Nano (Rev3.0)
  Part4 = Arduino Nano (Rev3.0)
  J15 = shrouded pin header, 10 pins [form="♂ (shrouded male)"]  # not connected
  S1 = H-Bridge with L298N
  J42 = double row male pin header, 20 pins [form="♂ (male)"]  # not connected
  J43 = double row male pin header, 20 pins [form="♂ (male)"]  # not connected
  J44 = double row male pin header, 20 pins [form="♂ (male)"]  # not connected
  J45 = shrouded pin header, 40 pins [form="♂ (shrouded male)"]  # not connected
  J1 = male pin header, 6 pins [form="♂ (male)"]
  J7 = male pin header, 2 pins [form="♂ (male)"]
  J6 = male pin header, 2 pins [form="♂ (male)"]
  J5 = male pin header, 2 pins [form="♂ (male)"]
  J4 = male pin header, 2 pins [form="♂ (male)"]
  Part5 = Arduino Nano (Rev3.0)
  Part6 = Arduino Nano (Rev3.0)
  J46 = male pin header, 6 pins [form="♂ (male)"]
  J47 = male pin header, 2 pins [form="♂ (male)"]
  J48 = male pin header, 2 pins [form="♂ (male)"]
  J49 = male pin header, 2 pins [form="♂ (male)"]
  J50 = male pin header, 2 pins [form="♂ (male)"]
  S2 = H-Bridge with L298N

nets:
  N1: Part3.D2, J7.pin1, J6.pin1
  N2: Part3.D3, J7.pin2, J6.pin2
  N3: Part3.D4, S1.ENA, J1.pin1
  N4: Part3.D10, S1.IN2, J1.pin3
  N5: Part3.D11/MOSI, S1.IN1, J1.pin2
  N6: Part4.D2, J5.pin1, J4.pin1
  N7: Part4.D3, J5.pin2, J4.pin2
  N8: Part4.D4, S1.ENB, J1.pin6
  N9: Part4.D10, S1.IN4, J1.pin5
  N10: Part4.D11/MOSI, S1.IN3, J1.pin4
  N11: Part5.D2, J49.pin1, J50.pin1
  N12: Part5.D3, J49.pin2, J50.pin2
  N13: Part5.D4, J46.pin1, S2.ENA
  N14: Part5.D10, J46.pin3, S2.IN2
  N15: Part5.D11/MOSI, J46.pin2, S2.IN1
  N16: Part6.D2, J47.pin1, J48.pin1
  N17: Part6.D3, J47.pin2, J48.pin2
  N18: Part6.D4, J46.pin6, S2.ENB
  N19: Part6.D10, J46.pin5, S2.IN4
  N20: Part6.D11/MOSI, J46.pin4, S2.IN3

notes:
  UAJ
  SKG
  SKF
  SKE

custom parts:
  H-Bridge with L298N: h-bridge
