# Fritzing sketch Layout_master_board (saved by Fritzing 0.9.3b)
perfboards: 1

parts:
  Part1 = Arduino Mega ADK (Rev3)  # not connected
  J3 = male pin header, 2 pins [form="♂ (male)"]
  J4 = male pin header, 2 pins [form="♂ (male)"]
  J5 = male pin header, 2 pins [form="♂ (male)"]  # not connected
  J6 = shrouded pin header, 10 pins [form="♂ (shrouded male)"]
  J7 = shrouded pin header, 10 pins [form="♂ (shrouded male)"]
  J8 = shrouded pin header, 10 pins [form="♂ (shrouded male)"]
  J1 = male pin header, 2 pins [form="♂ (male)"]
  J2 = male pin header, 4 pins [form="♂ (male)"]
  J10 = male pin header, 3 pins [form="♂ (male)"]
  J9 = male pin header, 2 pins [form="♂ (male)"]  # not connected

nets:
  N1: J3.pin1, J6.pin1, J7.pin1, J8.pin1
  N2: J3.pin2, J6.pin10, J7.pin10, J8.pin10
  N3: J4.pin2, J6.pin9
  N4: J6.pin3, J10.pin2
  N5: J6.pin4, J10.pin1
  N6: J6.pin7, J2.pin1
  N7: J6.pin8, J2.pin2
  N8: J7.pin3, J10.pin3
  N9: J7.pin8, J2.pin3
  N10: J8.pin2, J1.pin1
  N11: J8.pin3, J2.pin4
