# Fritzing sketch Layout_safety_board (saved by Fritzing 0.9.3b)
perfboards: 1

parts:
  R7 = Resistor [tolerance=±5% resistance=220 package=THT]
  S4 = Pushbutton [package=THT]
  S5 = Pushbutton [package=THT]
  LED4 = LED - 5mm [color="Red (633nm)" package="5 mm [THT]"]
  LED5 = LED - 5mm [color="Red (633nm)" package="5 mm [THT]"]
  J16 = male pin header, 4 pins [form="♂ (male)"]
  J17 = male pin header, 4 pins [form="♂ (male)"]
  J18 = male pin header, 4 pins [form="♂ (male)"]
  J19 = male pin header, 4 pins [form="♂ (male)"]
  J20 = male pin header, 4 pins [form="♂ (male)"]
  J21 = male pin header, 4 pins [form="♂ (male)"]
  F5 = FUSE [package=fuse_5mm]
  F6 = FUSE [package=fuse_5mm]
  F7 = FUSE [package=fuse_5mm]
  DS2Y-5-DC5V2 = DS2Y-5-DC5V [part_number=DS2Y-5-DC5V]
  J22 = female pin header, 3 pins [form="♀ (female)"]
  J23 = female pin header, 1 pin [form="♀ (female)"]
  J24 = female pin header, 1 pin [form="♀ (female)"]
  J25 = female pin header, 3 pins [form="♀ (female)"]
  C2 = Electrolytic Capacitor [capacitance=1µF package="100 mil [THT, electrolytic]"]
  R8 = Resistor [tolerance=±5% resistance=220 package=THT]
  J26 = female pin header, 1 pin [form="♀ (female)"]
  R9 = Resistor [tolerance=±5% resistance=220 package=THT]
  R10 = Resistor [tolerance=±5% resistance=220 package=THT]
  LED6 = LED - 5mm [color="Red (633nm)" package="5 mm [THT]"]
  F8 = FUSE [package=fuse_5mm]
  C3 = Electrolytic Capacitor [capacitance=1µF package="100 mil [THT, electrolytic]"]
  J34 = male pin header, 3 pins [form="♂ (male)"]
  J37 = female pin header, 1 pin [form="♀ (female)"]  # not connected
  J38 = Camdenboss CTB0158-3 [part_number=CTB0158-3 package=THT]
  J39 = female pin header, 5 pins [form="♀ (female)"]  # not connected
  J40 = female pin header, 5 pins [form="♀ (female)"]  # not connected
  J41 = female pin header, 5 pins [form="♀ (female)"]  # not connected
  J42 = female pin header, 5 pins [form="♀ (female)"]  # not connected
  J43 = female pin header, 5 pins [form="♀ (female)"]  # not connected
  J44 = female pin header, 5 pins [form="♀ (female)"]  # not connected
  J45 = female pin header, 5 pins [form="♀ (female)"]  # not connected
  J46 = female pin header, 5 pins [form="♀ (female)"]  # not connected
  J47 = female pin header, 5 pins [form="♀ (female)"]  # not connected
  J48 = female pin header, 5 pins [form="♀ (female)"]  # not connected
  J49 = female pin header, 5 pins [form="♀ (female)"]  # not connected
  J50 = Camdenboss CTB0158-2 [part_number=CTB0158-2 package=THT]
  U2 = mystery part, 22 pins [chip_label=?]
  J51 = male pin header, 3 pins [form="♂ (male)"]

nets:
  N1: R7.Pin_0, J16.pin4, J19.pin1, F7.2, DS2Y-5-DC5V2.6_N.C., J25.pin1
  N2: R7.Pin_1, LED4.anode
  N3: S4.leg0, S5.leg1, DS2Y-5-DC5V2.4_COM, J22.pin1
  N4: S4.leg1, DS2Y-5-DC5V2.1_+
  N5: S5.leg0, LED4.cathode, J20.pin1, J20.pin4, J21.pin4, J24.pin1, C2.-
  N6: LED5.cathode, J23.pin1
  N7: LED5.anode, R8.Pin_1
  N8: J16.pin1, J18.pin3
  N9: J16.pin2, J20.pin2, J20.pin3, J21.pin1, J21.pin2
  N10: J16.pin3, J17.pin3, J18.pin1, J18.pin4, J21.pin3, F6.1
  N11: J17.pin1, J18.pin2
  N12: J17.pin2, F6.2
  N13: J17.pin4, F5.2
  N14: F5.1, DS2Y-5-DC5V2.8_N.O., DS2Y-5-DC5V2.9_N.O., J25.pin2, C2.+, R8.Pin_0
  N15: DS2Y-5-DC5V2.16_-, R9.Pin_1
  N16: J26.pin1, R9.Pin_0
  N17: R10.Pin_1, LED6.anode
  N18: LED6.cathode, J50.pin1, J51.pin3
  N19: F8.1, C3.+, U2.pin11, U2.pin12
  N20: F8.2, J38.pin1
  N21: C3.-, J38.pin3, U2.pin19
  N22: J34.pin1, U2.pin22
  N23: J34.pin3, J51.pin1
  N24: J38.pin2, U2.pin15
  N25: J50.pin2, U2.pin1
