# Fritzing sketch Layout_slave_board (saved by Fritzing 0.9.3b)

parts:
  Part3 = Arduino Nano (Rev3.0)
  Part4 = Arduino Nano (Rev3.0)
  S1 = H-Bridge with L298N
  J42 = double row male pin header, 20 pins [form="♂ (male)"]
  J43 = double row male pin header, 20 pins [form="♂ (male)"]
  J44 = double row male pin header, 20 pins [form="♂ (male)"]
  J45 = shrouded pin header, 40 pins [form="♂ (shrouded male)"]  # not connected
  J1 = male pin header, 6 pins [form="♂ (male)"]
  J7 = male pin header, 2 pins [form="♂ (male)"]
  J6 = male pin header, 2 pins [form="♂ (male)"]
  J5 = male pin header, 2 pins [form="♂ (male)"]
  J4 = male pin header, 2 pins [form="♂ (male)"]
  Part5 = Arduino Nano (Rev3.0)
  Part6 = Arduino Nano (Rev3.0)
  J46 = male pin header, 6 pins [form="♂ (male)"]
  J47 = male pin header, 2 pins [form="♂ (male)"]
  J48 = male pin header, 2 pins [form="♂ (male)"]
  J49 = male pin header, 2 pins [form="♂ (male)"]
  J50 = male pin header, 2 pins [form="♂ (male)"]
  S2 = H-Bridge with L298N
  Part7 = Arduino Nano (Rev3.0)
  Part8 = Arduino Nano (Rev3.0)
  J51 = male pin header, 6 pins [form="♂ (male)"]
  J52 = male pin header, 2 pins [form="♂ (male)"]
  J53 = male pin header, 2 pins [form="♂ (male)"]
  J54 = male pin header, 2 pins [form="♂ (male)"]
  J55 = male pin header, 2 pins [form="♂ (male)"]
  S3 = H-Bridge with L298N
  J56 = shrouded pin header, 10 pins [form="♂ (shrouded male)"]
  J15 = shrouded pin header, 10 pins [form="♂ (shrouded male)"]
  J57 = male pin header, 1 pin [form="♂ (male)"]
  J58 = male pin header, 1 pin [form="♂ (male)"]
  J59 = shrouded pin header, 10 pins [form="♂ (shrouded male)"]  # not connected

nets:
  N1: Part3.D2, J42.pin6, J7.pin1, J6.pin1
  N2: Part3.D3, J44.pin15, J7.pin2, J6.pin2
  N3: Part3.D4, S1.ENA, J1.pin1
  N4: Part3.D10, S1.IN2, J1.pin3
  N5: Part3.D11/MOSI, S1.IN1, J1.pin2
  N6: Part4.D2, J42.pin9, J5.pin1, J4.pin1
  N7: Part4.D3, J44.pin12, J5.pin2, J4.pin2
  N8: Part4.D4, S1.ENB, J1.pin6
  N9: Part4.D10, S1.IN4, J1.pin5
  N10: Part4.D11/MOSI, S1.IN3, J1.pin4
  N11: S1.M1-01, J43.pin6
  N12: S1.M1-02, J44.pin6
  N13: S1.M2-01, J44.pin3
  N14: S1.M2-02, J43.pin3
  N15: J42.pin7, J15.pin9
  N16: J42.pin8, J15.pin10
  N17: J42.pin10, Part6.D2, J47.pin1, J48.pin1
  N18: J42.pin11, Part5.D2, J49.pin1, J50.pin1
  N19: J42.pin12, J42.pin13, J44.pin9, J58.pin1
  N20: J42.pin14, J44.pin7, J44.pin8, J57.pin1
  N21: J42.pin20, J43.pin1, S2.M1-01
  N22: J43.pin2, S2.M2-02
  N23: J43.pin4, J15.pin8
  N24: J43.pin5, J15.pin7
  N25: J44.pin1, S2.M1-02
  N26: J44.pin2, S2.M2-01
  N27: J44.pin4, J15.pin3
  N28: J44.pin5, J15.pin4
  N29: J44.pin10, Part5.D3, J49.pin2, J50.pin2
  N30: J44.pin11, Part6.D3, J47.pin2, J48.pin2
  N31: J44.pin13, J15.pin1
  N32: J44.pin14, J15.pin2
  N33: Part5.D4, J46.pin1, S2.ENA
  N34: Part5.D10, J46.pin3, S2.IN2
  N35: Part5.D11/MOSI, J46.pin2, S2.IN1
  N36: Part6.D4, J46.pin6, S2.ENB
  N37: Part6.D10, J46.pin5, S2.IN4
  N38: Part6.D11/MOSI, J46.pin4, S2.IN3
  N39: Part7.D2, J54.pin1, J55.pin1, J56.pin2
  N40: Part7.D3, J54.pin2, J55.pin2, J56.pin9
  N41: Part7.D4, J51.pin1, S3.ENA
  N42: Part7.D10, J51.pin3, S3.IN2
  N43: Part7.D11/MOSI, Part7.D12/MISO, J51.pin2, S3.IN1
  N44: Part8.D2, J52.pin1, J53.pin1, J56.pin1
  N45: Part8.D3, J52.pin2, J53.pin2, J56.pin10
  N46: Part8.D4, J51.pin6, S3.ENB
  N47: Part8.D10, J51.pin5, S3.IN4
  N48: Part8.D11/MOSI, Part8.D12/MISO, J51.pin4, S3.IN3
  N49: S3.M1-01, J56.pin4
  N50: S3.M1-02, J56.pin7
  N51: S3.M2-01, J56.pin8
  N52: S3.M2-02, J56.pin3

notes:
  UAJ
  SKG
  SKF
  SKE
  Shoulder
  UAE

custom parts:
  H-Bridge with L298N: h-bridge
