# Fritzing sketch Layout_slave_board_V2_comm (saved by Fritzing 0.9.3b)

parts:
  Part3 = Arduino Nano (Rev3.0)
  Part4 = Arduino Nano (Rev3.0)
  S1 = H-Bridge with L298N
  J44 = double row male pin header, 20 pins [form="♂ (male)"]
  J45 = shrouded pin header, 40 pins [form="♂ (shrouded male)"]  # not connected
  J1 = male pin header, 6 pins [form="♂ (male)"]
  J7 = male pin header, 2 pins [form="♂ (male)"]
  J6 = male pin header, 2 pins [form="♂ (male)"]
  J5 = male pin header, 2 pins [form="♂ (male)"]
  J4 = male pin header, 2 pins [form="♂ (male)"]
  Part5 = Arduino Nano (Rev3.0)
  Part6 = Arduino Nano (Rev3.0)
  J46 = male pin header, 6 pins [form="♂ (male)"]
  J47 = male pin header, 2 pins [form="♂ (male)"]
  J48 = male pin header, 2 pins [form="♂ (male)"]
  J49 = male pin header, 2 pins [form="♂ (male)"]
  J50 = male pin header, 2 pins [form="♂ (male)"]
  S2 = H-Bridge with L298N
  Part7 = Arduino Nano (Rev3.0)
  Part8 = Arduino Nano (Rev3.0)
  J51 = male pin header, 6 pins [form="♂ (male)"]
  J52 = male pin header, 2 pins [form="♂ (male)"]
  J53 = male pin header, 2 pins [form="♂ (male)"]
  J54 = male pin header, 2 pins [form="♂ (male)"]
  J55 = male pin header, 2 pins [form="♂ (male)"]
  S3 = H-Bridge with L298N
  J56 = shrouded pin header, 10 pins [form="♂ (shrouded male)"]
  J15 = shrouded pin header, 10 pins [form="♂ (shrouded male)"]
  J57 = male pin header, 1 pin [form="♂ (male)"]
  J58 = male pin header, 1 pin [form="♂ (male)"]
  D1 = Rectifier Diode [part_number=1N4001 package="300 mil [THT]"]
  D2 = Rectifier Diode [part_number=1N4001 package="300 mil [THT]"]
  D3 = Rectifier Diode [part_number=1N4001 package="300 mil [THT]"]
  D4 = Rectifier Diode [part_number=1N4001 package="300 mil [THT]"]
  J63 = male pin header, 1 pin [form="♂ (male)"]
  J64 = male pin header, 1 pin [form="♂ (male)"]
  J65 = male pin header, 1 pin [form="♂ (male)"]
  J66 = male pin header, 1 pin [form="♂ (male)"]
  R1 = Resistor [tolerance=±5% resistance=220 package=THT]
  J68 = male pin header, 1 pin [form="♂ (male)"]
  J69 = male pin header, 1 pin [form="♂ (male)"]
  D5 = Rectifier Diode [part_number=1N4001 package="300 mil [THT]"]
  J71 = male pin header, 1 pin [form="♂ (male)"]
  D6 = Rectifier Diode [part_number=1N4001 package="300 mil [THT]"]
  J74 = male pin header, 2 pins [form="♂ (male)"]
  J75 = male pin header, 2 pins [form="♂ (male)"]
  J76 = male pin header, 2 pins [form="♂ (male)"]
  J77 = male pin header, 2 pins [form="♂ (male)"]
  J78 = male pin header, 2 pins [form="♂ (male)"]
  J79 = male pin header, 2 pins [form="♂ (male)"]
  J80 = shrouded pin header, 10 pins [form="♂ (shrouded male)"]
  J81 = shrouded pin header, 10 pins [form="♂ (shrouded male)"]
  J43 = male pin header, 20 pins [form="♂ (male)"]
  J42 = male pin header, 20 pins [form="♂ (male)"]
  Part10 = Arduino Nano (Rev3.0)
  J83 = male pin header, 2 pins [form="♂ (male)"]
  J84 = male pin header, 2 pins [form="♂ (male)"]
  S4 = H-Bridge with L298N
  D8 = Rectifier Diode [part_number=1N4001 package="300 mil [THT]"]
  J88 = male pin header, 1 pin [form="♂ (male)"]
  J90 = male pin header, 2 pins [form="♂ (male)"]
  J92 = shrouded pin header, 10 pins [form="♂ (shrouded male)"]
  J82 = male pin header, 3 pins [form="♂ (male)"]
  J85 = male pin header, 4 pins [form="♂ (male)"]
  J93 = male pin header, 1 pin [form="♂ (male)"]
  J94 = male pin header, 1 pin [form="♂ (male)"]
  J95 = male pin header, 1 pin [form="♂ (male)"]
  J98 = male pin header, 1 pin [form="♂ (male)"]
  J99 = male pin header, 1 pin [form="♂ (male)"]
  J100 = male pin header, 1 pin [form="♂ (male)"]
  J101 = male pin header, 1 pin [form="♂ (male)"]
  J106 = female pin header, 2 pins [form="♀ (female)"]  # not connected
  J103 = male pin header, 8 pins [form="♂ (male)"]
  J102 = male pin header, 8 pins [form="♂ (male)"]
  J108 = male pin header, 2 pins [form="♂ (male)"]
  J109 = male pin header, 2 pins [form="♂ (male)"]
  J110 = male pin header, 2 pins [form="♂ (male)"]
  J111 = male pin header, 2 pins [form="♂ (male)"]
  J112 = male pin header, 2 pins [form="♂ (male)"]
  J113 = male pin header, 2 pins [form="♂ (male)"]
  J114 = male pin header, 2 pins [form="♂ (male)"]
  J115 = male pin header, 2 pins [form="♂ (male)"]
  J116 = male pin header, 2 pins [form="♂ (male)"]
  J117 = male pin header, 2 pins [form="♂ (male)"]
  J118 = male pin header, 2 pins [form="♂ (male)"]
  J119 = male pin header, 2 pins [form="♂ (male)"]
  J104 = female pin header, 10 pins [form="♀ (female)"]
  J105 = female pin header, 10 pins [form="♀ (female)"]
  U1 = mystery part, 8 pins [chip_label=?]  # not connected
  C1 = Ceramic Capacitor [capacitance=100nF voltage=16V package="100 mil [THT, multilayer]"]  # not connected

nets:
  N1: Part3.D1/TX, D3.cathode
  N2: Part3.D0/RX, J76.pin1
  N3: Part3.D2, J7.pin1, J6.pin1, J43.pin15, J42.pin6
  N4: Part3.D3, J44.pin15, J7.pin2, J6.pin2
  N5: Part3.D4, S1.ENA, J1.pin1
  N6: Part3.D10, S1.IN2, J1.pin3
  N7: Part3.D11/MOSI, S1.IN1, J1.pin2
  N8: Part3.D12/MISO, J80.pin7
  N9: Part4.D1/TX, D4.cathode
  N10: Part4.D0/RX, J77.pin1
  N11: Part4.D2, J5.pin1, J4.pin1, J43.pin12, J42.pin9
  N12: Part4.D3, J44.pin12, J5.pin2, J4.pin2
  N13: Part4.D4, S1.ENB, J1.pin6
  N14: Part4.D10, S1.IN4, J1.pin5
  N15: Part4.D11/MOSI, S1.IN3, J1.pin4
  N16: Part4.D12/MISO, J80.pin3
  N17: Part4.5V, R1.Pin_0
  N18: S1.M1-01, J43.pin6, J42.pin15
  N19: S1.M1-02, J44.pin6
  N20: S1.M2-01, J44.pin3
  N21: S1.M2-02, J43.pin3, J42.pin18
  N22: J44.pin1, S2.M1-02
  N23: J44.pin2, S2.M2-01
  N24: J44.pin4, J15.pin3
  N25: J44.pin5, J15.pin4
  N26: J44.pin7, J57.pin1, J43.pin7, J42.pin13, J42.pin14
  N27: J44.pin8, J44.pin9, J58.pin1, J43.pin9, J42.pin12
  N28: J44.pin10, Part5.D3, J49.pin2, J50.pin2
  N29: J44.pin11, Part6.D3, J47.pin2, J48.pin2
  N30: J44.pin13, J15.pin1
  N31: J44.pin14, J15.pin2
  N32: Part5.D1/TX, D1.cathode
  N33: Part5.D0/RX, J74.pin1
  N34: Part5.D2, J49.pin1, J50.pin1, J43.pin10, J42.pin11
  N35: Part5.D4, J46.pin1, S2.ENA, S2.ENA-5V
  N36: Part5.D10, J46.pin3, S2.IN2
  N37: Part5.D11/MOSI, J46.pin2, S2.IN1
  N38: Part5.D12/MISO, J80.pin8
  N39: Part6.D1/TX, D2.cathode
  N40: Part6.D0/RX, J75.pin1
  N41: Part6.D2, J47.pin1, J48.pin1, J43.pin11, J42.pin10
  N42: Part6.D4, J46.pin6, S2.ENB, S2.ENB-5V
  N43: Part6.D10, J46.pin5, S2.IN4
  N44: Part6.D11/MOSI, J46.pin4, S2.IN3
  N45: Part6.D12/MISO, J80.pin4
  N46: S2.M1-01, J43.pin1, J42.pin20
  N47: S2.M2-02, J43.pin2, J42.pin19
  N48: Part7.D1/TX, D6.cathode
  N49: Part7.D0/RX, J78.pin1
  N50: Part7.GND, Part7.D2, J54.pin1, J55.pin1, J56.pin2
  N51: Part7.D3, J54.pin2, J55.pin2, J56.pin9
  N52: Part7.D4, J51.pin1, S3.ENA, S3.ENA-5V
  N53: Part7.D9, Part7.D10, J51.pin3, S3.IN2
  N54: Part7.D11/MOSI, J51.pin2, S3.IN1
  N55: Part7.D12/MISO, J81.pin8
  N56: Part8.D0/RX, D5.cathode
  N57: Part8.RESET, J79.pin1
  N58: Part8.D2, J52.pin1, J53.pin1, J56.pin1
  N59: Part8.D3, J52.pin2, J53.pin2, J56.pin10
  N60: Part8.D4, J51.pin6, S3.ENB
  N61: Part8.D9, Part8.D10, J51.pin5, S3.IN4
  N62: Part8.D11/MOSI, J51.pin4, S3.IN3
  N63: Part8.D12/MISO, J81.pin3
  N64: S3.M1-01, J56.pin4
  N65: S3.M1-02, J56.pin7
  N66: S3.M2-01, J56.pin8
  N67: S3.M2-02, J56.pin3
  N68: J15.pin7, J43.pin5, J42.pin16
  N69: J15.pin8, J43.pin4, J42.pin17
  N70: J15.pin9, J43.pin14, J42.pin7
  N71: J15.pin10, J43.pin13, J42.pin8
  N72: D1.anode, D2.anode, D3.anode, D4.anode, J63.pin1, J64.pin1, J65.pin1, J66.pin1, R1.Pin_1, J68.pin1, J80.pin10
  N73: J69.pin1, D5.anode, J71.pin1, D6.anode, J81.pin10
  N74: J74.pin2, J75.pin2, J76.pin2, J77.pin2, J80.pin1
  N75: J78.pin2, J79.pin2, J81.pin1
  N76: J80.pin2, J101.pin1
  N77: J80.pin9, J100.pin1
  N78: J81.pin2, J99.pin1
  N79: J81.pin9, J98.pin1
  N80: Part10.D1/TX, D8.cathode
  N81: Part10.D0/RX, J90.pin1
  N82: Part10.D2, J83.pin1, J84.pin1, J85.pin2, J85.pin3, J93.pin1
  N83: Part10.D3, J83.pin2, J84.pin2, J85.pin4
  N84: Part10.D4, S4.ENA, S4.ENB, S4.ENA-5V, J82.pin3
  N85: Part10.D9, Part10.D10, S4.IN2, S4.IN4, J82.pin2
  N86: Part10.D11/MOSI, S4.IN1, S4.IN3, J82.pin1
  N87: Part10.D12/MISO, J92.pin3, J92.pin6
  N88: S4.M1-01, S4.M2-02
  N89: S4.M1-02, S4.M2-01
  N90: D8.anode, J92.pin10
  N91: J88.pin1, J85.pin1
  N92: J90.pin2, J92.pin1
  N93: J92.pin2, J94.pin1
  N94: J92.pin9, J95.pin1
  N95: J103.pin2, J114.pin2, J105.pin2
  N96: J103.pin3, J119.pin2, J105.pin3
  N97: J103.pin4, J118.pin2, J105.pin4
  N98: J103.pin5, J117.pin2, J105.pin5
  N99: J103.pin6, J115.pin2, J105.pin6
  N100: J103.pin7, J116.pin2, J105.pin7
  N101: J103.pin8, J105.pin10
  N102: J102.pin2, J108.pin1, J104.pin2
  N103: J102.pin3, J109.pin1, J104.pin3
  N104: J102.pin4, J110.pin1, J104.pin4
  N105: J102.pin5, J113.pin1, J104.pin5
  N106: J102.pin6, J112.pin1, J104.pin6
  N107: J102.pin7, J111.pin1, J104.pin7
  N108: J102.pin8, J104.pin10
  N109: J108.pin2, J111.pin2, J104.pin8
  N110: J114.pin1, J116.pin1, J105.pin8

notes:
  UAJ
  SKG
  SKF
  SKE
  Shoulder
  UAE
  Master
  10nF

custom parts:
  H-Bridge with L298N: h-bridge
