# Fritzing sketch SKE_Originalverkabelung (saved by Fritzing 0.9.2b)

parts:
  RP7 = Resistor [tolerance=±5% resistance=1k package=THT]
  RP8 = Resistor [tolerance=±5% resistance=1k package=THT]
  D5 = Rectifier Diode [part_number=1N4148 package="300 mil [THT]"]
  C7 = Ceramic Capacitor [capacitance=4.7nF package="100 mil [THT, multilayer]"]
  RP7_2 = Resistor [tolerance=±5% resistance=1k package=THT]
  RP8_2 = Resistor [tolerance=±5% resistance=1k package=THT]
  D6 = Rectifier Diode [part_number=1N4148 package="300 mil [THT]"]
  SKE-gelb = PHOTOTRANSISTOR REFLECTIVE OBJECT SENSOR [package=qrb1114-side]
  SKE-weis = PHOTOTRANSISTOR REFLECTIVE OBJECT SENSOR [package=qrb1114-side]
  C8 = Ceramic Capacitor [capacitance=4.7nF package="100 mil [THT, multilayer]"]
  M1 = DC Motor [part_number="DC Motor, 24V"]
  D7 = Rectifier Diode [part_number=BY206GP package="300 mil [THT]"]
  D8 = Rectifier Diode [part_number=BY206GP package="300 mil [THT]"]
  D9 = Rectifier Diode [part_number=BY206GP package="300 mil [THT]"]
  D10 = Rectifier Diode [part_number=BY206GP package="300 mil [THT]"]
  C9 = Ceramic Capacitor [capacitance=100nF part_number=104Z package="100 mil [THT, multilayer]"]
  C10 = Ceramic Capacitor [capacitance=680nF part_number=684 package="100 mil [THT, multilayer]"]
  R1 = Resistor [tolerance=±2% resistance=30 part_number=OSSGoO package=THT]
  R2 = Resistor [tolerance=±5% resistance=3.3 package=THT]

nets:
  5V: RP7.Pin_0, RP7_2.Pin_0
  N1: RP7.Pin_1, RP8.Pin_0, D5.anode, SKE-gelb.C
  N2: RP8.Pin_1, D5.cathode, C8.1
  GND: C7.0, SKE-gelb.E, SKE-weis.E, C8.0, C10.1, R2.Pin_1
  N3: C7.1, RP8_2.Pin_1, D6.cathode
  N4: RP7_2.Pin_1, RP8_2.Pin_0, D6.anode, SKE-weis.C
  L293E, Pin 8, Output2: M1.pin_1, D8.anode, D9.cathode, C9.1
  N5: M1.pin_2, D7.cathode, D10.anode, R1.Pin_1
  N6: D7.anode, D9.anode, R2.Pin_0
  24V: D8.cathode, D10.cathode
  N7: C9.0, C10.0, R1.Pin_0

notes:
  logic -->
  ~1.5m Leitung
